// Logisim project LC-2200-16.circ as structural Verilog: 4 circuits, main circuit main
module main (
  output [15:0] out_1
);

  wire C, comparator_1_eq, DrALU, DrMEM, DrOFF, DrPC, DrREG, LdA, LdB, LdIR, LdMAR, LdPC, LdZ, not_1_out,
       WrMEM, WrREG, z;
  wire [1:0] func;
  wire [3:0] regno;
  wire [4:0] SE;
  wire [15:0] alu_1_out, bit_extender_1_out, controlled_buffer_1_out, IR, ram_1_data, register_1_q,
       register_2_q, register_3_q, register_5_dout, register_6_q;

  Register #(.width(16)) register_1 (.D(controlled_buffer_1_out), .en(LdPC), .Q(register_1_q), .clk(C));  // open: clr
  assign controlled_buffer_1_out = DrPC ? register_1_q : 16'bz;  // Controlled_Buffer controlled_buffer_1
  Register #(.width(16)) register_2 (.D(controlled_buffer_1_out), .en(LdA), .Q(register_2_q), .clk(C));  // open: clr
  Register #(.width(16)) register_3 (.D(controlled_buffer_1_out), .en(LdB), .Q(register_3_q), .clk(C));  // open: clr
  ALU alu_1 (.A(register_2_q), .out(alu_1_out), .B(register_3_q), .func(func));
  assign controlled_buffer_1_out = DrALU ? alu_1_out : 16'bz;  // Controlled_Buffer controlled_buffer_2
  Comparator #(.width(16)) comparator_1 (
    .a(controlled_buffer_1_out), .b({16{1'b0}}), .eq(comparator_1_eq));  // open: gt, lt
  Register #(.width(1)) register_4 (.D(comparator_1_eq), .en(LdZ), .Q(z), .clk(C));  // open: clr
  register register_5 (
    .W(WrREG), .regno(regno), .Din(controlled_buffer_1_out), .C(C), .Dout(register_5_dout), .v0(out_1));
  assign controlled_buffer_1_out = DrREG ? register_5_dout : 16'bz;  // Controlled_Buffer controlled_buffer_3
  Clock clock_1 (.out(C));
  Register #(.width(16)) register_6 (.D(controlled_buffer_1_out), .en(LdMAR), .Q(register_6_q), .clk(C));  // open: clr
  MC mc_1 (
    .z(z), .IR(IR), .C(C), .imme(SE), .DrREG(DrREG), .DrMEM(DrMEM), .DrALU(DrALU), .DrPC(DrPC),
    .DrOFF(DrOFF), .LdPC(LdPC), .LdIR(LdIR), .LdMAR(LdMAR), .LdA(LdA), .LdB(LdB), .LdZ(LdZ), .WrREG(WrREG),
    .WrMEM(WrMEM), .func(func), .regno(regno));
  RAM #(.addrWidth(16), .dataWidth(16), .bus("separate")) ram_1 (
    .addr(register_6_q), .din(controlled_buffer_1_out), .data(ram_1_data), .str(WrMEM), .clk(C),
    .ld(not_1_out));  // open: sel, clr
  not not_1 (not_1_out, WrMEM);
  assign controlled_buffer_1_out = DrMEM ? ram_1_data : 16'bz;  // Controlled_Buffer controlled_buffer_4
  Register #(.width(16)) register_7 (.D(controlled_buffer_1_out), .en(LdIR), .Q(IR), .clk(C));  // open: clr
  assign bit_extender_1_out = {{11{SE[4]}}, SE};  // Bit_Extender bit_extender_1
  assign controlled_buffer_1_out = DrOFF ? bit_extender_1_out : 16'bz;  // Controlled_Buffer controlled_buffer_5

  // Other names for the same wires on the sheet: v0[15:0] = out_1

  // Notes on the sheet:
  //   Yang Yang
  //                yyang382
  //   PC
  //   LdA
  //   ALU
  //   LdB
  //   MAR
  //   IR
endmodule

module ALU (
  input  [15:0] A,
  input  [15:0] B,
  input  [1:0] func,
  output [15:0] out
);

  wire [15:0] ADD, minus, NAND, one;

  Adder #(.width(16)) adder_1 (.a(A), .b(B), .out(ADD));  // open: cin, cout
  Subtractor #(.width(16)) subtractor_1 (.a(A), .b(B), .out(minus));  // open: bin, bout
  Adder #(.width(16)) adder_2 (.a(A), .b(16'h1), .out(one));  // open: cin, cout
  assign NAND = ~(A & B);  // NAND_Gate nand_1, 16 bits wide
  Multiplexer #(.select(2), .width(16), .enable("false")) multiplexer_1 (
    .in0(ADD), .in1(NAND), .in2(minus), .in3(one), .out(out), .sel(func));
endmodule

module register (
  input  W,
  input  [3:0] regno,
  input  [15:0] Din,
  input  C,
  output [15:0] Dout,
  output [15:0] v0
);

  wire _0, _1, _2, _3, _4, _5, _6, _7, _8, _9, _10, _11, _12, _13, _14, _15;
  wire [15:0] a0_q, a1_q, a2_q, at_q, fp_q, k0_q, ra_q, s0_q, s1_q, s2_q, sp_q, t0_q, t1_q, t2_q,
       transistor_1_out, transistor_2_out, transistor_3_out, transistor_4_out, transistor_5_out,
       transistor_6_out, transistor_13_out, transistor_14_out, transistor_15_out, transistor_16_out,
       transistor_17_out, transistor_18_out, transistor_25_out, transistor_26_out, transistor_27_out,
       transistor_28_out, ZERO_q;

  Decoder #(.select(4), .enable("false")) decoder_1 (
    .out0(_0), .out1(_1), .out2(_2), .out3(_3), .out4(_4), .out5(_5), .out6(_6), .out7(_7), .out8(_8),
    .out9(_9), .out10(_10), .out11(_11), .out12(_12), .out13(_13), .out14(_14), .out15(_15), .sel(regno));
  Transistor #(.\type ("n"), .width(16)) transistor_1 (.in(Din), .out(transistor_1_out), .gate(_0));
  Transistor #(.\type ("n"), .width(16)) transistor_2 (.in(Din), .out(transistor_2_out), .gate(_1));
  Transistor #(.\type ("n"), .width(16)) transistor_3 (.in(Din), .out(transistor_3_out), .gate(_2));
  Register #(.width(16)) u_v0 (.D(transistor_3_out), .en(W), .Q(v0), .clk(C));  // open: clr
  Register #(.width(16)) a0 (.D(transistor_4_out), .en(W), .Q(a0_q), .clk(C));  // open: clr
  Transistor #(.\type ("n"), .width(16)) transistor_4 (.in(Din), .out(transistor_4_out), .gate(_3));
  Register #(.width(16)) a1 (.D(transistor_5_out), .en(W), .Q(a1_q), .clk(C));  // open: clr
  Transistor #(.\type ("n"), .width(16)) transistor_5 (.in(Din), .out(transistor_5_out), .gate(_4));
  Register #(.width(16)) a2 (.D(transistor_6_out), .en(W), .Q(a2_q), .clk(C));  // open: clr
  Transistor #(.\type ("n"), .width(16)) transistor_6 (.in(Din), .out(transistor_6_out), .gate(_5));
  Transistor #(.\type ("n"), .width(16)) transistor_7 (.in(ZERO_q), .out(Dout), .gate(_0));
  Register #(.width(16)) ZERO (.D(transistor_1_out), .en(W), .Q(ZERO_q), .clk(C));  // open: clr
  Register #(.width(16)) at (.D(transistor_2_out), .en(W), .Q(at_q), .clk(C));  // open: clr
  Transistor #(.\type ("n"), .width(16)) transistor_8 (.in(at_q), .out(Dout), .gate(_1));
  Transistor #(.\type ("n"), .width(16)) transistor_9 (.in(v0), .out(Dout), .gate(_2));
  Transistor #(.\type ("n"), .width(16)) transistor_10 (.in(a0_q), .out(Dout), .gate(_3));
  Transistor #(.\type ("n"), .width(16)) transistor_11 (.in(a1_q), .out(Dout), .gate(_4));
  Transistor #(.\type ("n"), .width(16)) transistor_12 (.in(a2_q), .out(Dout), .gate(_5));
  Register #(.width(16)) t0 (.D(transistor_13_out), .en(W), .Q(t0_q), .clk(C));  // open: clr
  Transistor #(.\type ("n"), .width(16)) transistor_13 (.in(Din), .out(transistor_13_out), .gate(_6));
  Register #(.width(16)) t1 (.D(transistor_14_out), .en(W), .Q(t1_q), .clk(C));  // open: clr
  Transistor #(.\type ("n"), .width(16)) transistor_14 (.in(Din), .out(transistor_14_out), .gate(_7));
  Register #(.width(16)) t2 (.D(transistor_15_out), .en(W), .Q(t2_q), .clk(C));  // open: clr
  Transistor #(.\type ("n"), .width(16)) transistor_15 (.in(Din), .out(transistor_15_out), .gate(_8));
  Transistor #(.\type ("n"), .width(16)) transistor_16 (.in(Din), .out(transistor_16_out), .gate(_9));
  Transistor #(.\type ("n"), .width(16)) transistor_17 (.in(Din), .out(transistor_17_out), .gate(_10));
  Register #(.width(16)) s2 (.D(transistor_18_out), .en(W), .Q(s2_q), .clk(C));  // open: clr
  Transistor #(.\type ("n"), .width(16)) transistor_18 (.in(Din), .out(transistor_18_out), .gate(_11));
  Transistor #(.\type ("n"), .width(16)) transistor_19 (.in(t0_q), .out(Dout), .gate(_6));
  Transistor #(.\type ("n"), .width(16)) transistor_20 (.in(t1_q), .out(Dout), .gate(_7));
  Transistor #(.\type ("n"), .width(16)) transistor_21 (.in(t2_q), .out(Dout), .gate(_8));
  Transistor #(.\type ("n"), .width(16)) transistor_22 (.in(s0_q), .out(Dout), .gate(_9));
  Register #(.width(16)) s0 (.D(transistor_16_out), .en(W), .Q(s0_q), .clk(C));  // open: clr
  Register #(.width(16)) s1 (.D(transistor_17_out), .en(W), .Q(s1_q), .clk(C));  // open: clr
  Transistor #(.\type ("n"), .width(16)) transistor_23 (.in(s1_q), .out(Dout), .gate(_10));
  Transistor #(.\type ("n"), .width(16)) transistor_24 (.in(s2_q), .out(Dout), .gate(_11));
  Register #(.width(16)) k0 (.D(transistor_25_out), .en(W), .Q(k0_q), .clk(C));  // open: clr
  Transistor #(.\type ("n"), .width(16)) transistor_25 (.in(Din), .out(transistor_25_out), .gate(_12));
  Register #(.width(16)) sp (.D(transistor_26_out), .en(W), .Q(sp_q), .clk(C));  // open: clr
  Transistor #(.\type ("n"), .width(16)) transistor_26 (.in(Din), .out(transistor_26_out), .gate(_13));
  Transistor #(.\type ("n"), .width(16)) transistor_27 (.in(Din), .out(transistor_27_out), .gate(_14));
  Register #(.width(16)) fp (.D(transistor_27_out), .en(W), .Q(fp_q), .clk(C));  // open: clr
  Register #(.width(16)) ra (.D(transistor_28_out), .en(W), .Q(ra_q), .clk(C));  // open: clr
  Transistor #(.\type ("n"), .width(16)) transistor_28 (.in(Din), .out(transistor_28_out), .gate(_15));
  Transistor #(.\type ("n"), .width(16)) transistor_29 (.in(k0_q), .out(Dout), .gate(_12));
  Transistor #(.\type ("n"), .width(16)) transistor_30 (.in(sp_q), .out(Dout), .gate(_13));
  Transistor #(.\type ("n"), .width(16)) transistor_31 (.in(fp_q), .out(Dout), .gate(_14));
  Transistor #(.\type ("n"), .width(16)) transistor_32 (.in(ra_q), .out(Dout), .gate(_15));
endmodule

module MC (
  input  z,
  input  [15:0] IR,
  input  C,
  output [4:0] imme,
  output DrREG,
  output DrMEM,
  output DrALU,
  output DrPC,
  output DrOFF,
  output LdPC,
  output LdIR,
  output LdMAR,
  output LdA,
  output LdB,
  output LdZ,
  output WrREG,
  output WrMEM,
  output [1:0] func,
  output [3:0] regno
);

  wire chkZ, OPTest, RSHi, RSLo;
  wire [5:0] multiplexer_1_out, NextS, register_1_q, rom_2_data, rom_3_data;

  ROM #(.addrWidth(6), .dataWidth(25)) rom_1 (
    .addr(register_1_q),
    .data({chkZ, OPTest, func, RSHi, RSLo, WrMEM, WrREG, LdZ, LdB, LdA, LdMAR, LdIR, LdPC, DrOFF, DrPC, DrALU, DrMEM, DrREG, NextS}));  // open: sel
  Register #(.width(6)) register_1 (.D(multiplexer_1_out), .Q(register_1_q), .clk(C));  // open: en, clr
  Multiplexer #(.select(2), .width(6), .enable("false")) multiplexer_1 (
    .in0(NextS), .in1(rom_2_data), .in2(rom_3_data), .out(multiplexer_1_out), .sel({chkZ, OPTest}));  // open: in3
  ROM #(.addrWidth(3), .dataWidth(6)) rom_2 (.addr(IR[15:13]), .data(rom_2_data));  // open: sel
  ROM #(.addrWidth(2), .dataWidth(6)) rom_3 (.addr({1'b0, z}), .data(rom_3_data));  // open: sel
  Multiplexer #(.select(2), .width(4), .enable("false")) multiplexer_2 (
    .in0(IR[12:9]), .in1(IR[8:5]), .in2(IR[4:1]), .out(regno), .sel({RSHi, RSLo}));  // open: in3

  assign imme = IR[4:0];

  // Other names for the same wires on the sheet: ALULo = func[0]; ALUHi = func[1]; RX[3:0] = IR[12:9];
  //   OPcode[2:0] = IR[15:13]; RY[3:0] = IR[8:5]; RZ[3:0] = IR[4:1]

  // Notes on the sheet:
  //   contents of rom_1 (hex, n*v repeats v):
  //   6201 1082 e00900 84044 108045 20100 84047 8408 20100 8404a 10804b 220100 8404d 840e 210f 20080 84051
  //   8412 2113 40040 4055 88056 410117 1000000 4219 841a 900 0 a021d 840 1e
  //   contents of rom_2 (hex, n*v repeats v):
  //   3 9 6 c 10 14 1c 1e
  //   contents of rom_3 (hex, n*v repeats v):
  //   1b 18
endmodule
